// Logisim project jk flip floop.circ as structural Verilog: 1 circuit, main circuit main
module main (
  input  in_1,
  input  in_2,
  input  in_3,
  output out_4,
  output out_5
);

  wire and_1_out, and_2_out, and_3_out, and_4_out, and_5_out, and_6_out, clock_1_out, clock_2_out, nor_1_out,
       nor_2_out, not_1_out;

  Clock clock_1 (.out(clock_1_out));
  Clock clock_2 (.out(clock_2_out));
  and and_1 (and_1_out, out_4, in_1, clock_1_out);
  and and_2 (and_2_out, clock_1_out, in_2, out_5);
  and and_3 (and_3_out, in_3, clock_2_out);
  and and_4 (and_4_out, clock_2_out, in_3);
  nor nor_1 (nor_1_out, and_1_out, nor_2_out);
  nor nor_2 (nor_2_out, nor_1_out, and_2_out);
  not not_1 (not_1_out, clock_1_out);
  and and_5 (and_5_out, nor_1_out, not_1_out);
  and and_6 (and_6_out, not_1_out, nor_2_out);
  nor nor_3 (out_4, and_5_out, out_5);
  nor nor_4 (out_5, out_4, and_6_out);

  // Notes on the sheet:
  //   JK flip floop
endmodule
