// Logisim project sr,d flip floop.circ as structural Verilog: 1 circuit, main circuit main
module main (
  input  in_1,
  input  in_2,
  input  in_3,
  input  in_4
);

  wire and_1_out, and_2_out, clock_1_out, nand_1_out, nand_2_out, nand_3_out, nand_4_out, nor_1_out,
       nor_2_out, not_1_out;

  Clock clock_1 (.out(clock_1_out));
  not not_1 (not_1_out, in_4);
  and and_1 (and_1_out, in_2, in_3);
  nand nand_1 (nand_1_out, in_4, in_4, clock_1_out);
  nand nand_2 (nand_2_out, clock_1_out, not_1_out);
  and and_2 (and_2_out, in_1, in_2);
  nor nor_1 (nor_1_out, and_2_out, nor_2_out);
  nand nand_3 (nand_3_out, nand_1_out, nand_1_out, nand_4_out);
  nand nand_4 (nand_4_out, nand_3_out, nand_2_out);
  nor nor_2 (nor_2_out, nor_1_out, and_1_out);
  LED led_1 (.in(nor_1_out));
  LED led_2 (.in(nor_2_out));
  LED led_3 (.in(nand_3_out));
  LED led_4 (.in(nand_4_out));

  // Notes on the sheet:
  //   SR flip floop
  //   D flip floop
endmodule
